# Fritzing sketch Bicyduino fritzing (saved by Fritzing 0.9.2b)
breadboards: 1

parts:
  Pro_Micro1 = Pro Micro
  S2 = Reed switch [package=THT]
  TFT1 = 2.2" TFT with MicroSD Breakout
  GY1 = MPU-6050 Board GY-521 [form="♀ (female)" package=THT]

nets:
  GND: Pro_Micro1.GND, TFT1.GND
  N1: Pro_Micro1.D2, S2.pin_2
  N2: Pro_Micro1.D8, TFT1.RST
  N3: Pro_Micro1.D10, TFT1.CS
  N4: Pro_Micro1.D18/A0, GY1.pin4
  N5: Pro_Micro1.D19/A1, GY1.pin3
  VCC: Pro_Micro1.VCC, S2.pin_1, TFT1.VIN, GY1.pin1, GY1.pin2

custom parts:
  Pro Micro: The SparkFun Pro Micro is a complete USB-based microcontoller development system, in a very small footprint, capable of implementing many types of projects. All programming can be done via the USB port.
  2.2" TFT with MicroSD Breakout: 2.2" TFT Display with HX8340B Controller and MicroSD Card
  MPU-6050 Board GY-521: Acelerometro y Giroscopio MPU-6050 Board GY-521
